# Fritzing sketch Wiring - fritzing save (saved by Fritzing 0.9.9b)
breadboards: 1

parts:
  Part1 = Arduino Mega 2560 (Rev3)
  LCD1 = LCD screen
  U1 = NodeMCU V1.0
  Keypad4x1 = Keypad Membran 4x4
  LED1 = LED - 5mm [color="Green (560nm)" current=0.030 package="5 mm [THT]"]
  LED2 = LED - 5mm [color="Red (633nm)" current=0.030 package="5 mm [THT]"]
  R1 = Resistor [tolerance=±5% resistance=200 package="0402 [SMD]"]
  R2 = Resistor [tolerance=±5% resistance=200 package="0402 [SMD]"]
  Part2 = RFID-RC522-v2

nets:
  N1: Part1.D10_PWM, LED1.anode
  N2: Part1.D9_PWM, LED2.anode
  3V3: Part1.3V3, Part2.3.3V
  5V: Part1.5V, LCD1.VDD, LCD1.LED+, U1.Vin
  GND: Part1.GND, LCD1.VSS, LCD1.V0, LCD1.R/W, LCD1.LED-, U1.GND, R1.Pin_1, R2.Pin_1, Part2.GND
  N3: Part1.D1_TX0, U1.RX
  N4: Part1.D2_PWM, LCD1.RS
  N5: Part1.D3_PWM, LCD1.E
  N6: Part1.D4_PWM, LCD1.DB4
  N7: Part1.D5_PWM, LCD1.DB5
  N8: Part1.D6_PWM, LCD1.DB6
  N9: Part1.D7_PWM, LCD1.DB7
  N10: Part1.D23, Keypad4x1.Pin8
  N11: Part1.D25, Keypad4x1.Pin7
  N12: Part1.D27, Keypad4x1.Pin6
  N13: Part1.D29, Keypad4x1.Pin5
  N14: Part1.D31, Keypad4x1.Pin4
  N15: Part1.D33, Keypad4x1.Pin3
  N16: Part1.D35, Keypad4x1.Pin2
  N17: Part1.D37, Keypad4x1.Pin1
  N18: Part1.D48, Part2.RST
  N19: Part1.D50, Part2.MISO
  N20: Part1.D51, Part2.MOSI
  N21: Part1.D52, Part2.SCK
  N22: Part1.D53, Part2.SDA
  N23: LED1.cathode, R1.Pin_0
  N24: LED2.cathode, R2.Pin_0

custom parts:
  NodeMCU V1.0: ESP8266 based NodeMCU
  Keypad Membran 4x4: Membrane Keypad 4x4 Matrix
  RFID-RC522-v2: A simple China made RFID-RC522 Reader; do check the pin labels, as this is a MFRC522 based clone.
