# Fritzing sketch Wiring - fritzing save (saved by Fritzing 0.9.9b)

parts:
  U1 = NodeMCU V1.0
  KY-1 = Keyes Relay [package=THT]
  M1 = Dagu DGServo 9g (Top view) [part_number=RS001B]
  VCC1 = Battery block 9V

nets:
  N1: U1.D0, M1.pulse
  N2: U1.D1, KY-1.signal
  N3: U1.3V3, KY-1.power, KY-1.C
  GND: U1.GND, KY-1.ground, M1.gnd, VCC1.-
  N4: U1.Vin, VCC1.+
  N5: KY-1.NO, M1.vcc

custom parts:
  NodeMCU V1.0: ESP8266 based NodeMCU
  Keyes Relay: The Keyes 5V relay module is suitable for SCM development, home appliance control. It uses a 5V~12V TIL control signal which can control DC / AC signal.
